// Logisim project cpu.circ as structural Verilog: 7 circuits, main circuit main
// CPU
module main (
  input  [31:0] RS_READ_VALUE,
  input  [31:0] RI_READ_VALUE,
  input  [31:0] RD_READ_VALUE,
  input  [31:0] JC_READ_VALUE,
  input  [31:0] INSTRUCTION,
  input  CLOCK,
  output [4:0] RS,
  output [4:0] RI,
  output [4:0] RD,
  output [31:0] RD_WRITE_VALUE,
  output RD_WRITE_ENABLE,
  output [23:0] FETCH_ADDRESS
);

  wire and_2_out, ext_op, jal_inst, jeq, jge, jgt, jle, jlt, jne, jump, mem_wrte, memory_to_reg, nPC_sel,
       perform_jump, word_mode, write_to_reg;
  wire [2:0] and_1_out, bit_extender_1_out;
  wire [3:0] alu_control;
  wire [23:0] adder_1_out, adder_2_out, bit_extender_5_out, multiplexer_5_out, multiplexer_7_out;
  wire [24:0] bit_extender_4_out;
  wire [31:0] bit_extender_2_out, bit_extender_3_out, bit_extender_6_out, intermediate, multiplexer_2_out,
       multiplexer_8_out, u_alu_1_alu_result, u_mem_1_data_out;

  Multiplexer #(.width(5)) multiplexer_1 (
    .in0(INSTRUCTION[26:22]), .in1(5'b00110), .out(RD), .sel(jal_inst));  // open: en
  or or_1 (RD_WRITE_ENABLE, write_to_reg, jal_inst);
  Register #(.width(24)) PC (.D(multiplexer_7_out), .Q(FETCH_ADDRESS), .clk(CLOCK));  // open: en, clr
  assign bit_extender_1_out = {{2{jump}}, jump};  // Bit_Extender bit_extender_1
  assign bit_extender_2_out = {{15{1'b0}}, INSTRUCTION[16:0]};  // Bit_Extender bit_extender_2
  assign bit_extender_3_out = {{15{INSTRUCTION[16]}}, INSTRUCTION[16:0]};  // Bit_Extender bit_extender_3
  Multiplexer #(.width(32)) multiplexer_2 (
    .in0(RI_READ_VALUE), .in1(intermediate), .out(multiplexer_2_out), .sel(INSTRUCTION[27]));  // open: en
  Multiplexer #(.select(3)) multiplexer_3 (
    .in0(1'b1), .in1(jgt), .in2(jeq), .in3(jlt), .in4(jle), .in5(jne), .in6(jge), .in7(1'b1),
    .out(perform_jump), .sel(INSTRUCTION[26:24]));  // open: en
  assign and_1_out = INSTRUCTION[26:24] & bit_extender_1_out;  // AND_Gate and_1, 3 bits wide
  Comparator #(.width(3)) comparator_1 (.a(and_1_out), .b(3'b111), .eq(jal_inst));  // open: gt, lt
  Multiplexer #(.width(32)) multiplexer_4 (
    .in0(bit_extender_2_out), .in1(bit_extender_3_out), .out(intermediate), .sel(ext_op));  // open: en
  u_ALU u_alu_1 (
    .ALU_X(RS_READ_VALUE), .ALU_Y(multiplexer_2_out), .ALU_RESULT(u_alu_1_alu_result),
    .ALU_CONTROL(alu_control));
  Adder #(.width(24)) adder_1 (.a(FETCH_ADDRESS), .b(24'h1), .out(adder_1_out));  // open: cin, cout
  Bit_Extender #(.in_width(32), .out_width(25)) bit_extender_4 (.in(u_alu_1_alu_result), .out(bit_extender_4_out));
  Bit_Extender #(.in_width(32), .out_width(24)) bit_extender_5 (.in(RI_READ_VALUE), .out(bit_extender_5_out));
  and and_2 (and_2_out, perform_jump, jump);
  Multiplexer #(.width(24)) multiplexer_5 (
    .in0(bit_extender_5_out), .in1(INSTRUCTION[23:0]), .out(multiplexer_5_out), .sel(INSTRUCTION[27]));  // open: en
  Comparator #(.width(32)) comparator_2 (.a(JC_READ_VALUE), .b({32{1'b0}}), .gt(jgt), .eq(jeq), .lt(jlt));
  or or_2 (jle, jeq, jlt);
  not not_1 (jne, jeq);
  or or_3 (jge, jeq, jgt);
  Multiplexer #(.select(4), .width(7), .enable("false")) multiplexer_6 (
    .in0(7'b0011000), .in1(7'b0011000), .in2(7'b0011000), .in3(7'b0011000), .in4(7'b0011000),
    .in5(7'b0011000), .in6(7'b0011000), .in7(7'b0011000), .in8(7'b0011000), .in9(7'b0011000),
    .in10(7'b0011100), .in11(7'b0010010), .in12(7'b0111100), .in13(7'b0110010), .in14(7'b0011000),
    .in15(7'b1000001), .out({jump, word_mode, ext_op, write_to_reg, memory_to_reg, mem_wrte, nPC_sel}),
    .sel(INSTRUCTION[31:28]));
  u_MEM u_mem_1 (
    .ADDRESS(bit_extender_4_out), .WORD_MODE(word_mode), .MEM_WRITE(mem_wrte), .DATA_IN(RD_READ_VALUE),
    .CLOCK(CLOCK), .DATA_OUT(u_mem_1_data_out));
  Multiplexer #(.width(24)) multiplexer_7 (
    .in0(adder_1_out), .in1(multiplexer_5_out), .out(multiplexer_7_out), .sel(and_2_out));  // open: en
  assign bit_extender_6_out = {{8{1'b0}}, adder_2_out};  // Bit_Extender bit_extender_6
  Adder #(.width(24)) adder_2 (.a(FETCH_ADDRESS), .b(24'h1), .out(adder_2_out));  // open: cin, cout
  Multiplexer #(.width(32)) multiplexer_8 (
    .in0(u_alu_1_alu_result), .in1(u_mem_1_data_out), .out(multiplexer_8_out), .sel(memory_to_reg));  // open: en
  Multiplexer #(.width(32)) multiplexer_9 (
    .in0(multiplexer_8_out), .in1(bit_extender_6_out), .out(RD_WRITE_VALUE), .sel(jal_inst));  // open: en
  Multiplexer #(.select(4), .width(4)) multiplexer_10 (
    .in0(4'b0000), .in1(4'b0001), .in2(4'b0010), .in3(4'b0011), .in4(4'b0100), .in5(4'b0101), .in6(4'b0110),
    .in7(4'b0111), .in8(4'b1000), .in9(4'b1001), .in10(4'b0110), .in11(4'b0110), .in12(4'b0110),
    .in13(4'b0110), .in14(4'b1110), .in15(4'b0000), .out(alu_control), .sel(INSTRUCTION[31:28]));  // open: en

  assign RI = INSTRUCTION[4:0];
  assign RS = INSTRUCTION[21:17];

  // Other names for the same wires on the sheet: clk = CLOCK; jump_address[23:0] = INSTRUCTION[23:0];
  //   RD_t[4:0] = INSTRUCTION[26:22]; _27thbit = INSTRUCTION[27]; jc_val[31:0] = JC_READ_VALUE;
  //   pc_val[23:0] = FETCH_ADDRESS; rd_val[31:0] = RD_READ_VALUE; rd_write_val[31:0] = RD_WRITE_VALUE;
  //   ri_val[31:0] = RI_READ_VALUE; rs_val[31:0] = RS_READ_VALUE
endmodule

module u_ALU (
  input  [31:0] ALU_X,
  input  [31:0] ALU_Y,
  input  [3:0] ALU_CONTROL,
  output [31:0] ALU_RESULT
);

  wire equal, larger, not_1_out, rdequal, rdless, riless;
  wire [4:0] bit_extender_1_out;
  wire [31:0] adder_1_out, and_1_out, corrected_rd, corrected_rs, divresult, minmax, multiplexer_5_out,
       multiplier_1_out, multiplier_2_out, multiplier_3_out, multiplier_4_out, multiplier_5_out, or_1_out,
       preresult, rszero, secondaryresult, subtractor_1_out, u_rev_1_output, u_sla_1_out, u_slr_1_out,
       xor_1_out;

  Multiplexer #(.width(32)) multiplexer_1 (
    .in0(32'h80000000), .in1(32'h7fffffff), .out(minmax), .sel(larger));  // open: en
  Multiplier #(.width(32)) multiplier_1 (.a(ALU_X), .b({32{1'b1}}), .out(multiplier_1_out));  // open: cin, cout
  Multiplexer #(.width(32)) multiplexer_2 (
    .in0(ALU_X), .in1(multiplier_1_out), .out(corrected_rd), .sel(rdless));  // open: en
  Multiplexer #(.width(32)) multiplexer_3 (.in0(minmax), .in1({32{1'b0}}), .out(rszero), .sel(rdequal));  // open: en
  Multiplier #(.width(32)) multiplier_2 (.a(ALU_Y), .b({32{1'b1}}), .out(multiplier_2_out));  // open: cin, cout
  Comparator #(.width(32)) comparator_1 (.a(ALU_X), .b({32{1'b0}}), .gt(larger), .eq(rdequal), .lt(rdless));
  Comparator #(.width(32)) comparator_2 (.a(ALU_Y), .b({32{1'b0}}), .eq(equal), .lt(riless));  // open: gt
  Multiplexer #(.width(32)) multiplexer_4 (
    .in0(ALU_Y), .in1(multiplier_2_out), .out(corrected_rs), .sel(riless));  // open: en
  u_sla u_sla_1 (.IN(ALU_X), .amount(ALU_Y), .OUT(u_sla_1_out));
  u_slr u_slr_1 (.IN(ALU_X), .amount(ALU_Y), .OUT(u_slr_1_out));
  assign and_1_out = ALU_X & ALU_Y;  // AND_Gate and_1, 32 bits wide
  assign or_1_out = ALU_X | ALU_Y;  // OR_Gate or_1, 32 bits wide
  assign xor_1_out = ALU_X ^ ALU_Y;  // XOR_Gate xor_1, 32 bits wide
  Multiplier #(.width(32)) multiplier_3 (.a(ALU_X), .b(ALU_Y), .out(multiplier_3_out));  // open: cin, cout
  Divider #(.width(32)) divider_1 (.a(corrected_rd), .b(corrected_rs), .out(divresult));  // open: upper, rem
  Bit_Extender #(.in_width(32), .out_width(5)) bit_extender_1 (.in(ALU_Y), .out(bit_extender_1_out));
  Adder #(.width(32)) adder_1 (.a(ALU_X), .b(ALU_Y), .out(adder_1_out));  // open: cin, cout
  Subtractor #(.width(32)) subtractor_1 (.a(ALU_X), .b(ALU_Y), .out(subtractor_1_out));  // open: bin, bout
  Multiplier #(.width(32)) multiplier_4 (
    .a(secondaryresult), .b({32{1'b1}}), .out(multiplier_4_out));  // open: cin, cout
  u_REV u_rev_1 (.INPUT(ALU_X), .OUTPUT(u_rev_1_output), .REVERSE_AMOUNT(bit_extender_1_out));
  Multiplexer #(.width(32)) multiplexer_5 (
    .in0(secondaryresult), .in1(multiplier_4_out), .out(multiplexer_5_out), .sel(riless));  // open: en
  Multiplexer #(.width(32)) multiplexer_6 (
    .in0(rszero), .in1(divresult), .out(preresult), .sel(not_1_out));  // open: en
  not not_1 (not_1_out, equal);
  Multiplier #(.width(32)) multiplier_5 (.a(preresult), .b({32{1'b1}}), .out(multiplier_5_out));  // open: cin, cout
  Multiplexer #(.width(32)) multiplexer_7 (
    .in0(preresult), .in1(multiplier_5_out), .out(secondaryresult), .sel(rdless));  // open: en
  Multiplexer #(.select(4), .width(32)) multiplexer_8 (
    .in0(u_sla_1_out), .in1(u_slr_1_out), .in2(and_1_out), .in3(or_1_out), .in4(u_rev_1_output),
    .in5(xor_1_out), .in6(adder_1_out), .in7(subtractor_1_out), .in8(multiplier_3_out),
    .in9(multiplexer_5_out), .in14({ALU_Y[16:0], ALU_X[14:0]}), .out(ALU_RESULT), .sel(ALU_CONTROL));  // open: in10, in11, in12, in13, in15, en

  // Other names for the same wires on the sheet: rd_val[31:0] = ALU_X; rs_val[31:0] = ALU_Y
endmodule

// Data Memory
module u_MEM (
  input  [24:0] ADDRESS,
  input  WORD_MODE,
  input  MEM_WRITE,
  input  [31:0] DATA_IN,
  input  CLOCK,
  output [31:0] DATA_OUT
);

  wire not_1_out, not_2_out, or_1_out, or_2_out;
  wire [15:0] evendata, odddata;
  wire [23:0] adder_1_out, evenaddress;
  wire [31:0] _00, _01, _10;

  Multiplexer #(.width(24)) multiplexer_1 (
    .in0(ADDRESS[24:1]), .in1(adder_1_out), .out(evenaddress), .sel(ADDRESS[0]));  // open: en
  Adder #(.width(24)) adder_1 (.a(ADDRESS[24:1]), .b(24'h1), .out(adder_1_out));  // open: cin, cout
  Multiplexer #(.width(16)) multiplexer_2 (
    .in0(DATA_IN[15:0]), .in1(DATA_IN[31:16]), .out(evendata), .sel(ADDRESS[0]));  // open: en
  Multiplexer #(.width(16)) multiplexer_3 (
    .in0(DATA_IN[15:0]), .in1(DATA_IN[31:16]), .out(odddata), .sel(not_1_out));  // open: en
  not not_1 (not_1_out, ADDRESS[0]);
  or or_1 (or_1_out, WORD_MODE, not_2_out);
  not not_2 (not_2_out, ADDRESS[0]);
  assign _00 = {{16{1'b0}}, _01[15:0]};  // Bit_Extender bit_extender_1
  assign _10 = {{16{1'b0}}, _01[31:16]};  // Bit_Extender bit_extender_2
  RAM #(.addrWidth(24), .dataWidth(16), .bus("separate")) ram_1 (
    .addr(evenaddress), .din(evendata), .data(_01[15:0]), .str(MEM_WRITE), .sel(or_1_out), .clk(CLOCK));  // open: ld, clr
  Multiplexer #(.select(2), .width(32)) multiplexer_4 (
    .in0(_00), .in1(_01), .in2(_10), .in3({_01[15:0], _01[31:16]}), .out(DATA_OUT),
    .sel({ADDRESS[0], WORD_MODE}));  // open: en
  or or_2 (or_2_out, WORD_MODE, ADDRESS[0]);
  RAM #(.addrWidth(24), .dataWidth(16), .bus("separate")) ram_2 (
    .addr(ADDRESS[24:1]), .din(odddata), .data(_01[31:16]), .str(MEM_WRITE), .sel(or_2_out), .clk(CLOCK));  // open: ld, clr

  // Other names for the same wires on the sheet: wrd_mode = WORD_MODE; zerobit = ADDRESS[0];
  //   _11[31:0] = {_01[15:0], _01[31:16]}; oddoutput[15:0] = _01[31:16]; evenoutput[15:0] = _01[15:0];
  //   oddaddress[23:0] = ADDRESS[24:1]; clk = CLOCK
endmodule

module u_REV (
  input  [31:0] INPUT,
  input  [4:0] REVERSE_AMOUNT,
  output [31:0] OUTPUT
);

  wire [4:0] bit_extender_1_out, bit_extender_2_out, bit_extender_3_out, bit_extender_4_out,
       bit_extender_5_out, shifter_1_out, shifter_2_out, shifter_3_out, shifter_4_out, shifter_5_out;
  wire [31:0] u_reverse_help_1_out_3, u_reverse_help_2_out_3, u_reverse_help_3_out_3, u_reverse_help_5_out_3;

  assign bit_extender_1_out = {{4{1'b0}}, REVERSE_AMOUNT[0]};  // Bit_Extender bit_extender_1
  assign bit_extender_2_out = {{4{1'b0}}, REVERSE_AMOUNT[1]};  // Bit_Extender bit_extender_2
  assign bit_extender_3_out = {{4{1'b0}}, REVERSE_AMOUNT[2]};  // Bit_Extender bit_extender_3
  assign bit_extender_4_out = {{4{1'b0}}, REVERSE_AMOUNT[3]};  // Bit_Extender bit_extender_4
  assign bit_extender_5_out = {{4{1'b0}}, REVERSE_AMOUNT[4]};  // Bit_Extender bit_extender_5
  u_reverse_help u_reverse_help_1 (.A(INPUT), .B(shifter_1_out), .out_3(u_reverse_help_1_out_3));
  Shifter #(.width(5)) shifter_1 (.in(bit_extender_1_out), .\dist (3'b000), .out(shifter_1_out));
  Shifter #(.width(5)) shifter_2 (.in(bit_extender_2_out), .\dist (3'b001), .out(shifter_2_out));
  Shifter #(.width(5)) shifter_3 (.in(bit_extender_3_out), .\dist (3'b010), .out(shifter_3_out));
  Shifter #(.width(5)) shifter_4 (.in(bit_extender_4_out), .\dist (3'b011), .out(shifter_4_out));
  Shifter #(.width(5)) shifter_5 (.in(bit_extender_5_out), .\dist (3'b100), .out(shifter_5_out));
  u_reverse_help u_reverse_help_2 (.A(u_reverse_help_3_out_3), .B(shifter_3_out), .out_3(u_reverse_help_2_out_3));
  u_reverse_help u_reverse_help_3 (.A(u_reverse_help_1_out_3), .B(shifter_2_out), .out_3(u_reverse_help_3_out_3));
  u_reverse_help u_reverse_help_4 (.A(u_reverse_help_5_out_3), .B(shifter_5_out), .out_3(OUTPUT));
  u_reverse_help u_reverse_help_5 (.A(u_reverse_help_2_out_3), .B(shifter_4_out), .out_3(u_reverse_help_5_out_3));
endmodule

module u_reverse_help (
  input  [31:0] A,
  input  [4:0] B,
  output [31:0] out_3
);

  Multiplexer #(.select(5), .width(32)) multiplexer_1 (
    .in0(A),
    .in1({A[30], A[31], A[28], A[29], A[26], A[27], A[24], A[25], A[22], A[23], A[20], A[21], A[18], A[19], A[16], A[17], A[14], A[15], A[12], A[13], A[10], A[11], A[8], A[9], A[6], A[7], A[4], A[5], A[2], A[3], A[0], A[1]}),
    .in2({A[29:28], A[31:30], A[25:24], A[27:26], A[21:20], A[23:22], A[17:16], A[19:18], A[13:12], A[15:14], A[9:8], A[11:10], A[5:4], A[7:6], A[1:0], A[3:2]}),
    .in4({A[27:24], A[31:28], A[19:16], A[23:20], A[11:8], A[15:12], A[3:0], A[7:4]}),
    .in8({A[23:16], A[31:24], A[7:0], A[15:8]}), .in16({A[15:0], A[31:16]}), .out(out_3), .sel(B));  // open: in3, in5, in6, in7, in9, in10, in11, in12, in13, in14, in15, in17, in18, in19, in20, in21, in22, in23, in24, in25, in26, in27, in28, in29, in30, in31, en
endmodule

module u_sla (
  input  [31:0] IN,
  input  [31:0] amount,
  output [31:0] OUT
);

  wire biton;
  wire [0:0] multiplexer_2_out;
  wire [1:0] multiplexer_3_out;
  wire [3:0] multiplexer_5_out;
  wire [7:0] multiplexer_7_out;
  wire [15:0] multiplexer_10_out;
  wire [31:0] multiplexer_1_out, multiplexer_4_out, multiplexer_6_out, multiplexer_8_out;

  or or_1 (biton, 1'b0, IN[0]);
  Multiplexer #(.width(32)) multiplexer_1 (
    .in0(IN), .in1({IN[30:0], multiplexer_2_out[0]}), .out(multiplexer_1_out), .sel(amount[0]));  // open: en
  Multiplexer multiplexer_2 (.in0(1'b0), .in1(1'b1), .out(multiplexer_2_out[0]), .sel(biton));  // open: en
  Multiplexer #(.width(2)) multiplexer_3 (.in0(2'b00), .in1(2'b11), .out(multiplexer_3_out), .sel(biton));  // open: en
  Multiplexer #(.width(32)) multiplexer_4 (
    .in0(multiplexer_1_out), .in1({multiplexer_1_out[29:0], multiplexer_3_out}), .out(multiplexer_4_out),
    .sel(amount[1]));  // open: en
  Multiplexer #(.width(4)) multiplexer_5 (
    .in0(4'b0000), .in1(4'b1111), .out(multiplexer_5_out), .sel(biton));  // open: en
  Multiplexer #(.width(32)) multiplexer_6 (
    .in0(multiplexer_4_out), .in1({multiplexer_4_out[27:0], multiplexer_5_out}), .out(multiplexer_6_out),
    .sel(amount[2]));  // open: en
  Multiplexer #(.width(8)) multiplexer_7 (
    .in0({8{1'b0}}), .in1({8{1'b1}}), .out(multiplexer_7_out), .sel(biton));  // open: en
  Multiplexer #(.width(32)) multiplexer_8 (
    .in0(multiplexer_6_out), .in1({multiplexer_6_out[23:0], multiplexer_7_out}), .out(multiplexer_8_out),
    .sel(amount[3]));  // open: en
  Multiplexer #(.width(32)) multiplexer_9 (
    .in0(multiplexer_8_out), .in1({multiplexer_8_out[15:0], multiplexer_10_out}), .out(OUT), .sel(amount[4]));  // open: en
  Multiplexer #(.width(16)) multiplexer_10 (
    .in0({16{1'b0}}), .in1({16{1'b1}}), .out(multiplexer_10_out), .sel(biton));  // open: en

  // Other names for the same wires on the sheet: zerobit = amount[0]; onebit = amount[1]; secondbit = amount[2];
  //   thirdbit = amount[3]; fourthbit = amount[4]
endmodule

module u_slr (
  input  [31:0] IN,
  input  [31:0] amount,
  output [31:0] OUT
);

  wire biton;
  wire [1:0] multiplexer_4_out;
  wire [3:0] multiplexer_6_out;
  wire [7:0] multiplexer_7_out;
  wire [15:0] multiplexer_9_out;
  wire [31:0] multiplexer_2_out, multiplexer_3_out, multiplexer_5_out, multiplexer_8_out;
  wire [31:31] multiplexer_1_out;

  or or_1 (biton, 1'b0, IN[31]);
  Multiplexer multiplexer_1 (.in0(1'b0), .in1(1'b1), .out(multiplexer_1_out[31]), .sel(biton));  // open: en
  Multiplexer #(.width(32)) multiplexer_2 (
    .in0(IN), .in1({multiplexer_1_out[31], IN[31:1]}), .out(multiplexer_2_out), .sel(amount[0]));  // open: en
  Multiplexer #(.width(32)) multiplexer_3 (
    .in0(multiplexer_2_out), .in1({multiplexer_4_out, multiplexer_2_out[31:2]}), .out(multiplexer_3_out),
    .sel(amount[1]));  // open: en
  Multiplexer #(.width(2)) multiplexer_4 (.in0(2'b00), .in1(2'b11), .out(multiplexer_4_out), .sel(biton));  // open: en
  Multiplexer #(.width(32)) multiplexer_5 (
    .in0(multiplexer_3_out), .in1({multiplexer_6_out, multiplexer_3_out[31:4]}), .out(multiplexer_5_out),
    .sel(amount[2]));  // open: en
  Multiplexer #(.width(4)) multiplexer_6 (
    .in0(4'b0000), .in1(4'b1111), .out(multiplexer_6_out), .sel(biton));  // open: en
  Multiplexer #(.width(8)) multiplexer_7 (
    .in0({8{1'b0}}), .in1({8{1'b1}}), .out(multiplexer_7_out), .sel(biton));  // open: en
  Multiplexer #(.width(32)) multiplexer_8 (
    .in0(multiplexer_5_out), .in1({multiplexer_7_out, multiplexer_5_out[31:8]}), .out(multiplexer_8_out),
    .sel(amount[3]));  // open: en
  Multiplexer #(.width(16)) multiplexer_9 (
    .in0({16{1'b0}}), .in1({16{1'b1}}), .out(multiplexer_9_out), .sel(biton));  // open: en
  Multiplexer #(.width(32)) multiplexer_10 (
    .in0(multiplexer_8_out), .in1({multiplexer_9_out, multiplexer_8_out[31:16]}), .out(OUT), .sel(amount[4]));  // open: en

  // Other names for the same wires on the sheet: zerobit = amount[0]; onebit = amount[1]; secondbit = amount[2];
  //   thirdbit = amount[3]; fourthbit = amount[4]
endmodule
